# Fritzing sketch raspberry_pi_pico_v2 (saved by Fritzing 0.9.9b)
breadboards: 1

parts:
  Part2 = HTU21D Breakout
  BMP280_Breakout1 = BMP280 Breakout Board [part_number=BMP280]
  Mod2 = Raspberry Pi Pico
  U1 = ESP8266 WiFi Module [part_number=ESP8266]
  IC1 = DS1307 [package=THT]
  R1 = Resistor [tolerance=±5% resistance=10k package=THT]
  C1 = Capacitor [package=cap-pth-small2]
  BAT5 = Battery Holders [package=battcom_20mm_pth]
  R3 = Resistor [tolerance=±5% resistance=10k package=THT]
  Y2 = CRYSTAL [package=crystal-32khz-smd]

nets:
  N1: Part2.SCL, BMP280_Breakout1.SCL, Mod2.pin_2, IC1.SCL_-_I2C_Clock, R1.Pin_1
  N2: Part2.SDA, BMP280_Breakout1.SDA, Mod2.pin_1, IC1.SDA_-_I2C_Data, R3.Pin_1
  GND: Part2.GND, BMP280_Breakout1.GND, Mod2.pin_3, Mod2.pin_8, Mod2.pin_13, Mod2.pin_18, Mod2.pin_23, Mod2.pin_28, Mod2.pin_33, Mod2.pin_38, U1.GND, IC1.0V, C1.1, BAT5.+
  VCC: Part2.3.3V, BMP280_Breakout1.VCC, Mod2.pin_36, U1.VCC, U1.CH_PD
  N3: Mod2.pin_6, U1.RXD
  N4: Mod2.pin_7, U1.TXD
  N5: Mod2.pin_40, IC1.+V, R1.Pin_0, C1.2, R3.Pin_0
  N6: IC1.X1_-_Crystal, Y2.1, Y2.2
  N7: IC1.Vbat_-_Backup_Supply, BAT5.-

custom parts:
  HTU21D Breakout: This is a breadboard friendly breakout board for the Measurement Specialties high-precision, low-power digital humidity sensor.
  BMP280 Breakout Board: This is a breakout board for the Bosch Sensortec BMP280, "an absolute barometric pressure sensor especially designed for mobile applications." The operation range is 300 to 1100 hPa. Supply voltage is 1.2 to 3.6V. Operating temperature range is -40 to +85 °C.
  Raspberry Pi Pico: Raspberry Pi Pico. Based around the RP2040 microcontroller the Pico is a low cost microcontroller device bringing Raspberry Pi quality, cost, and easy of use to the microcontroller space. Jan 2021, Split part in to two versions: tht (this one) and SMD. This one will drill holes for a .1 in header in pcb to allow plugging in the module as well as providing pads to solder the module to the top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
  ESP8266 WiFi Module: Generic WiFi Module based on the ESP8266 with onboard PCB antenna and UART communications
